# Fritzing sketch pokey (saved by Fritzing 0.9.2b)
breadboards: 2

parts:
  Part1 = Arduino Nano (Rev3.0)
  POKEY = IC, DIP package, 40 pins [chip_label=IC]
  AMP1 = GF1002 Stereo Amplifier
  Oscillator = IC, DIP package, 4 pins [chip_label=IC]
  R1 = Resistor [tolerance=±5% resistance=10k package=THT]
  C1 = Electrolytic Capacitor [capacitance=1µF package="100 mil [THT, electrolytic]"]
  J1 = Piezo Speaker

nets:
  N1: Part1.GND, POKEY.pin1, AMP1.POWER-, AMP1.INPUTG, Oscillator.pin2
  N2: Part1.D9, POKEY.pin36
  N3: Part1.D10, POKEY.pin35
  N4: Part1.D11/MOSI, POKEY.pin34
  N5: Part1.D12/MISO, POKEY.pin33
  N6: Part1.5V, POKEY.pin17, AMP1.POWER+, Oscillator.pin4, R1.Pin_1
  N7: Part1.A7, POKEY.pin6
  N8: Part1.A6, POKEY.pin5
  N9: Part1.A5, POKEY.pin4
  N10: Part1.A4, POKEY.pin3
  N11: Part1.A3, POKEY.pin2
  N12: Part1.A2, POKEY.pin40
  N13: Part1.A1, POKEY.pin39
  N14: Part1.A0, POKEY.pin38
  N15: Part1.D13/SCK, POKEY.pin30
  N16: POKEY.pin7, Oscillator.pin3
  N17: POKEY.pin37, R1.Pin_0, C1.+
  N18: AMP1.ROUT-, J1.pin1
  N19: AMP1.ROUT+, J1.pin2
  N20: AMP1.INPUTR, C1.-

custom parts:
  GF1002 Stereo Amplifier: GF1002 6 Watt Stereo Amplifier
